# Fritzing sketch Proyecto casa inteligente  (saved by Fritzing 0.9.3b)
breadboards: 4

parts:
  R1 = Resistor [tolerance=±5% resistance=1k package=THT]
  R2 = Resistor [tolerance=±5% resistance=2.2k package=THT]
  Componente1 = Arduino Uno (Rev3)
  U2 = ESP32-38PinWide [part_number=ESP32-38PinWide]
  Part2 = KY-003 Hall Magnetic Sensor Module [package="Breakout board"]
  Part4 = KY-016 RGB Full Color LED Module [package="Breakout board"]
  Part5 = KY-017 Mercury Tilt Switch [package="Breakout board"]
  Part6 = KY-026 Flame Sensor Module [package="Breakout board"]
  Mic2 = KY-038
  Part7 = KY-006 Passive Buzzer Module [package="Breakout board"]
  R3 = Rotary Potentiometer (Small) [maximum_resistance=100kΩ package=THT]
  Part8 = KY-009 Full Color RGB LED SMD Module [package="Breakout board"]
  Part9 = KY-015 Temperature & Humidity Sensor Module [package="Breakout board"]

nets:
  N1: R1.Pin_0, Componente1.D8
  N2: R1.Pin_1, R2.Pin_1
  N3: R2.Pin_0, U2.GPIO5
  N4: Componente1.A0, U2.GPIO4
  N5: Componente1.A1, Mic2.pin1
  N6: Componente1.A2, Mic2.pin4
  N7: Componente1.A3, R3.wiper
  N8: Componente1.A4/SDA, Part6.A0
  N9: Componente1.D9_PWM, Part8.G
  N10: Componente1.D10_PWM/SS, Part8.B
  N11: Componente1.D11_PWM/MOSI, Part4.R
  N12: Componente1.D2, Part9.S
  N13: Componente1.D3_PWM, Part5.S
  N14: Componente1.D4, Part2.S
  N15: Componente1.D6_PWM, Part8.R
  N16: Componente1.D7, Part7.S
  N17: Componente1.5V, Part6.+
  GND: Componente1.GND, U2.GND, Part6.G
  VIN: Part2.Vin, Part5.Vin, Mic2.pin3, R3.leg1
  N18: Part2.-, Part5.-, Mic2.pin2, R3.leg2
  N19: Part4.-, Part8.-, Part9.-

custom parts:
  ESP32-38PinWide: Generic 38-Pin ESP32 with wide format (only access to one side of pins on a breadboard) based on Stephen Lilley's HiLetgo ESP-WROOM-32 ESP32 ESP-32S Development Board.
  KY-003 Hall Magnetic Sensor Module: KEYES KY-003 Arduino Hall Magnetic Sensor Module is a switch that will turn on/off in the presence of a magnetic field.
  KY-016 RGB Full Color LED Module: KY-016 Arduino full color 5mm RGB LED, different colors can be obtained by mixing the three primary colors.
  KY-017 Mercury Tilt Switch: Arduino KY-017 mercury tilt switch module, it uses a small mercury ball that completes the circuit when you tilt the module.
  KY-026 Flame Sensor Module: KEYES KY-026 Arduino Flame Sensor Module reacts iin the presence of fire.
  KY-038: ky-038 Microphone sound sensor module
  KY-006 Passive Buzzer Module: Passive Piezoelectric Buzzer Module Keyes KY-006, it can produce a range of sound tones depending on the input frequency.
  KY-009 Full Color RGB LED SMD Module: RGB full color LED Module KY-009 for Arduino, emits a range of colors by mixing red, green and blue. The amount of each primary color is adjusted using PWM.
  KY-015 Temperature & Humidity Sensor Module: KY-015 temperature and humidity sensor module, provides a low-latency serial interface to measure humidity and temperature.
